// Digital circuit RegFile.dig as structural Verilog
module RegFile (
  input  [31:0] DataIN,
  input  [4:0] Bus_A_Select,
  input  Write,
  input  [4:0] Bus_B_Select,
  input  [4:0] Input_Select,
  output [31:0] BusA,
  output [31:0] BusB
);

  wire CS_1, CS_2, CS_3, CS_4, CS_5, CS_6, CS_7, CS_8, CS_9, CS_10, CS_11, CS_12, CS_13, CS_14, CS_15, CS_16,
       CS_17, CS_18, CS_19, CS_20, CS_21, CS_22, CS_23, CS_24, CS_25, CS_26, CS_27, CS_28, CS_29, CS_30,
       decoder_1_out_0, decoder_1_out_1, decoder_1_out_2, decoder_1_out_3, decoder_1_out_4, decoder_1_out_5,
       decoder_1_out_6, decoder_1_out_7, decoder_1_out_8, decoder_1_out_9, decoder_1_out_10,
       decoder_1_out_11, decoder_1_out_12, decoder_1_out_13, decoder_1_out_14, decoder_1_out_15,
       decoder_1_out_16, decoder_1_out_17, decoder_1_out_18, decoder_1_out_19, decoder_1_out_20,
       decoder_1_out_21, decoder_1_out_22, decoder_1_out_23, decoder_1_out_24, decoder_1_out_25,
       decoder_1_out_26, decoder_1_out_27, decoder_1_out_28, decoder_1_out_29, decoder_1_out_30,
       decoder_1_out_31, decoder_3_out_30, decoder_3_out_31, register_1_p5, register_2_p5, register_3_p5,
       register_4_p5, register_5_p5, register_6_p5, register_7_p5, register_8_p5, register_9_p5,
       register_10_p5, register_11_p5, register_12_p5, register_13_p5, register_14_p5, register_15_p5,
       register_16_p5, register_17_p5, register_18_p5, register_19_p5, register_20_p5, register_21_p5,
       register_22_p5, register_23_p5, register_24_p5, register_25_p5, register_26_p5, register_27_p5,
       register_28_p5, register_29_p5, register_30_p5;
  wire [4:0] not_1_out;

  Decoder #(.Selector_Bits(5)) decoder_1 (
    .sel(Bus_A_Select), .out_0(decoder_1_out_0), .out_1(decoder_1_out_1), .out_2(decoder_1_out_2),
    .out_3(decoder_1_out_3), .out_4(decoder_1_out_4), .out_5(decoder_1_out_5), .out_6(decoder_1_out_6),
    .out_7(decoder_1_out_7), .out_8(decoder_1_out_8), .out_9(decoder_1_out_9), .out_10(decoder_1_out_10),
    .out_11(decoder_1_out_11), .out_12(decoder_1_out_12), .out_13(decoder_1_out_13),
    .out_14(decoder_1_out_14), .out_15(decoder_1_out_15), .out_16(decoder_1_out_16),
    .out_17(decoder_1_out_17), .out_18(decoder_1_out_18), .out_19(decoder_1_out_19),
    .out_20(decoder_1_out_20), .out_21(decoder_1_out_21), .out_22(decoder_1_out_22),
    .out_23(decoder_1_out_23), .out_24(decoder_1_out_24), .out_25(decoder_1_out_25),
    .out_26(decoder_1_out_26), .out_27(decoder_1_out_27), .out_28(decoder_1_out_28),
    .out_29(decoder_1_out_29), .out_30(decoder_1_out_30), .out_31(decoder_1_out_31));
  Decoder #(.Selector_Bits(5)) decoder_2 (
    .sel(Input_Select), .out_2(CS_1), .out_3(CS_2), .out_4(CS_3), .out_5(CS_4), .out_6(CS_5), .out_7(CS_6),
    .out_8(CS_7), .out_9(CS_8), .out_10(CS_9), .out_11(CS_10), .out_12(CS_11), .out_13(CS_12),
    .out_14(CS_13), .out_15(CS_14), .out_16(CS_15), .out_17(CS_16), .out_18(CS_17), .out_19(CS_18),
    .out_20(CS_19), .out_21(CS_20), .out_22(CS_21), .out_23(CS_22), .out_24(CS_23), .out_25(CS_24),
    .out_26(CS_25), .out_27(CS_26), .out_28(CS_27), .out_29(CS_28), .out_30(CS_29), .out_31(CS_30));  // open: out_0, out_1
  // Register register_1: pin names not known; wires that end beside it: DataIN, Write, CS_1, decoder_1_out_2, register_1_p5, BusA, BusB
  // Register register_2: pin names not known; wires that end beside it: DataIN, Write, CS_2, decoder_1_out_3, register_2_p5, BusA, BusB
  // Register register_3: pin names not known; wires that end beside it: DataIN, Write, CS_3, decoder_1_out_4, register_3_p5, BusA, BusB
  // Register register_4: pin names not known; wires that end beside it: DataIN, Write, CS_4, decoder_1_out_5, register_4_p5, BusA, BusB
  // Register register_5: pin names not known; wires that end beside it: DataIN, Write, CS_5, decoder_1_out_6, register_5_p5, BusA, BusB
  // Register register_6: pin names not known; wires that end beside it: DataIN, Write, CS_6, decoder_1_out_7, register_6_p5, BusA, BusB
  // Register register_7: pin names not known; wires that end beside it: DataIN, Write, CS_7, decoder_1_out_8, register_7_p5, BusA, BusB
  // Register register_8: pin names not known; wires that end beside it: DataIN, Write, CS_8, decoder_1_out_9, register_8_p5, BusA, BusB
  // Register register_9: pin names not known; wires that end beside it: DataIN, Write, CS_9, decoder_1_out_10, register_9_p5, BusA, BusB
  // Register register_10: pin names not known; wires that end beside it: DataIN, Write, CS_10, decoder_1_out_11, register_10_p5, BusA, BusB
  // Register register_11: pin names not known; wires that end beside it: DataIN, Write, CS_11, decoder_1_out_12, register_11_p5, BusA, BusB
  // Register register_12: pin names not known; wires that end beside it: DataIN, Write, CS_12, decoder_1_out_13, register_12_p5, BusA, BusB
  // Register register_13: pin names not known; wires that end beside it: DataIN, Write, CS_13, decoder_1_out_14, register_13_p5, BusA, BusB
  // Register register_14: pin names not known; wires that end beside it: DataIN, Write, CS_14, decoder_1_out_15, register_14_p5, BusA, BusB
  // Register register_15: pin names not known; wires that end beside it: DataIN, Write, CS_15, decoder_1_out_16, register_15_p5, BusA, BusB
  // Register register_16: pin names not known; wires that end beside it: DataIN, Write, CS_16, decoder_1_out_17, register_16_p5, BusA, BusB
  // Register register_17: pin names not known; wires that end beside it: DataIN, Write, CS_17, decoder_1_out_18, register_17_p5, BusA, BusB
  // Register register_18: pin names not known; wires that end beside it: DataIN, Write, CS_18, decoder_1_out_19, register_18_p5, BusA, BusB
  // Register register_19: pin names not known; wires that end beside it: DataIN, Write, CS_19, decoder_1_out_20, register_19_p5, BusA, BusB
  // Register register_20: pin names not known; wires that end beside it: DataIN, Write, CS_20, decoder_1_out_21, register_20_p5, BusA, BusB
  // Register register_21: pin names not known; wires that end beside it: DataIN, Write, CS_21, decoder_1_out_22, register_21_p5, BusA, BusB
  // Register register_22: pin names not known; wires that end beside it: DataIN, Write, CS_22, decoder_1_out_23, register_22_p5, BusA, BusB
  // Register register_23: pin names not known; wires that end beside it: DataIN, Write, CS_23, decoder_1_out_24, register_23_p5, BusA, BusB
  // Register register_24: pin names not known; wires that end beside it: DataIN, Write, CS_24, decoder_1_out_25, register_24_p5, BusA, BusB
  // Register register_25: pin names not known; wires that end beside it: DataIN, Write, CS_25, decoder_1_out_26, register_25_p5, BusA, BusB
  // Register register_26: pin names not known; wires that end beside it: DataIN, Write, CS_26, decoder_1_out_27, register_26_p5, BusA, BusB
  // Register register_27: pin names not known; wires that end beside it: DataIN, Write, CS_27, decoder_1_out_28, register_27_p5, BusA, BusB
  // Register register_28: pin names not known; wires that end beside it: DataIN, Write, CS_28, decoder_1_out_29, register_28_p5, BusA, BusB
  // Register register_29: pin names not known; wires that end beside it: DataIN, Write, CS_29, decoder_1_out_30, register_29_p5, BusA, BusB
  // Register register_30: pin names not known; wires that end beside it: DataIN, Write, CS_30, decoder_1_out_31, register_30_p5, BusA, BusB
  assign BusA = decoder_1_out_0 ? {32{1'b0}} : 32'bz;  // Driver driver_1
  assign BusA = decoder_1_out_1 ? 32'h1 : 32'bz;  // Driver driver_2
  assign BusB = decoder_3_out_31 ? {32{1'b0}} : 32'bz;  // Driver driver_3
  assign BusB = decoder_3_out_30 ? 32'h1 : 32'bz;  // Driver driver_4
  assign not_1_out = ~Bus_B_Select;  // Not not_1, 5 bits wide
  Decoder #(.Selector_Bits(5)) decoder_3 (
    .sel(not_1_out), .out_0(register_30_p5), .out_1(register_29_p5), .out_2(register_28_p5),
    .out_3(register_27_p5), .out_4(register_26_p5), .out_5(register_25_p5), .out_6(register_24_p5),
    .out_7(register_23_p5), .out_8(register_22_p5), .out_9(register_21_p5), .out_10(register_20_p5),
    .out_11(register_19_p5), .out_12(register_18_p5), .out_13(register_17_p5), .out_14(register_16_p5),
    .out_15(register_15_p5), .out_16(register_14_p5), .out_17(register_13_p5), .out_18(register_12_p5),
    .out_19(register_11_p5), .out_20(register_10_p5), .out_21(register_9_p5), .out_22(register_8_p5),
    .out_23(register_7_p5), .out_24(register_6_p5), .out_25(register_5_p5), .out_26(register_4_p5),
    .out_27(register_3_p5), .out_28(register_2_p5), .out_29(register_1_p5), .out_30(decoder_3_out_30),
    .out_31(decoder_3_out_31));
endmodule
