// Digital circuit Register.dig as structural Verilog
module Register (
  input  EnBusA,
  input  EnBusB,
  input  [31:0] Data,
  input  Write,
  input  CS,
  output [31:0] BusA,
  output [31:0] BusB
);

  wire [31:0] register_1_q;

  Register #(.Bits(32)) register_1 (.D(Data), .C(Write), .en(CS), .Q(register_1_q));
  assign BusA = EnBusA ? register_1_q : 32'bz;  // Driver driver_1
  assign BusB = EnBusB ? register_1_q : 32'bz;  // Driver driver_2
endmodule
